// Logisim project 2to4decoder.circ as structural Verilog: 1 circuit, main circuit main
module main (
  input  i0,
  input  i1,
  output o00,
  output o01,
  output o10,
  output o11
);

  wire not_1_out, not_2_out;

  not not_1 (not_1_out, i0);
  not not_2 (not_2_out, i1);
  and and_1 (o00, not_1_out, not_2_out);
  and and_2 (o01, not_1_out, i1);
  and and_3 (o10, i0, not_2_out);
  and and_4 (o11, i0, i1);
endmodule
