// Logisim project 3saturate.circ as structural Verilog: 16 circuits, main circuit main
module main (
  input  down,
  input  clear
);

  wire clock_1_out, out_1_bot, out_1_lbot, out_1_ltop, out_1_mid, out_1_rbot, out_1_rtop, out_1_top;
  wire [2:0] next_q2_prime, register_1_q;

  Clock clock_1 (.out(clock_1_out));
  next next (
    .d(down), .q2(register_1_q[0]), .q1(register_1_q[1]), .q0(register_1_q[2]), .q2_prime(next_q2_prime[0]),
    .q1_prime(next_q2_prime[1]), .q0_prime(next_q2_prime[2]));
  Register #(.width(3)) register_1 (.D(next_q2_prime), .en(1'b1), .Q(register_1_q), .clk(clock_1_out), .clr(clear));
  out out_1 (
    .q2(register_1_q[0]), .q1(register_1_q[1]), .q0(register_1_q[2]), .top(out_1_top), .ltop(out_1_ltop),
    .rtop(out_1_rtop), .mid(out_1_mid), .lbot(out_1_lbot), .rbot(out_1_rbot), .bot(out_1_bot));
  _7_Segment_Display u_7_segment_display_1 (
    .g(out_1_mid), .f(out_1_ltop), .a(out_1_top), .b(out_1_rtop), .e(out_1_lbot), .d(out_1_bot),
    .c(out_1_rbot));  // open: dp

  // Notes on the sheet:
  //   DOWN? = 0: Counts upward, does not wrap around.
  //   DOWN? = 1: Counts down, does not wrap around.
endmodule

module next (
  input  d,
  input  q2,
  input  q1,
  input  q0,
  output q2_prime,
  output q1_prime,
  output q0_prime
);

  wire down_q2_logic_1_q2_prime, q0_logic_1_q0_prime, q0_prime_logic_down_q0_prime, q1_logic_1_q1_prime,
       q1_prime_down_logic_q1_prime, q2_logic_1_q2_prime;

  q2_logic q2_logic_1 (.d(d), .in_2(q2), .q1(q1), .q0(q0), .q2_prime(q2_logic_1_q2_prime));
  down_q2_logic down_q2_logic_1 (.d(q2), .q2(q2), .q1(q1), .q0(q0), .q2_prime(down_q2_logic_1_q2_prime));
  q1_logic q1_logic_1 (.d(d), .q2(q2), .q1(q1), .q0(q0), .q1_prime(q1_logic_1_q1_prime));
  down_q1_logic q1_prime_down_logic (.d(d), .q2(q2), .q1(q1), .q0(q0), .q1_prime(q1_prime_down_logic_q1_prime));
  q0_logic q0_logic_1 (.d(d), .q2(q2), .q1(q1), .q0(q0), .q0_prime(q0_logic_1_q0_prime));
  down_q0_logic q0_prime_logic_down (.d(d), .q2(q2), .q1(q1), .q0(q0), .q0_prime(q0_prime_logic_down_q0_prime));
  or or_1 (q2_prime, q2_logic_1_q2_prime, down_q2_logic_1_q2_prime);
  or or_2 (q1_prime, q1_logic_1_q1_prime, q1_prime_down_logic_q1_prime);
  or or_3 (q0_prime, q0_logic_1_q0_prime, q0_prime_logic_down_q0_prime);

  // Notes on the sheet:
  //   q2' logic_up
  //   q2' logic_down
  //   q1' logic_up
  //   q0' logic_up
endmodule

module out (
  input  q2,
  input  q1,
  input  q0,
  output top,
  output ltop,
  output rtop,
  output mid,
  output lbot,
  output rbot,
  output bot
);

  top_logic top_logic_1 (.q2(q2), .q1(q1), .q0(q0), .top(top));
  ltop_logic ltop_logic_1 (.q2(q2), .q1(q1), .q0(q0), .ltop(ltop));
  rtop_logic rtop_logic_1 (.q2(q2), .q1(q1), .q0(q0), .ltop(rtop));
  mid_logic mid_logic_1 (.q2(q2), .q1(q1), .q0(q0), .mid(mid));
  lbot_logic lbot_logic_1 (.q2(q2), .q1(q1), .q0(q0), .lbot(lbot));
  rbot_logic rbot_logic_1 (.q2(q2), .q1(q1), .q0(q0), .rbot(rbot));
  bot_logic bot_logic_1 (.q2(q2), .q1(q1), .q0(q0), .lbot(bot));
endmodule

module down_q2_logic (
  input  d,
  input  q2,
  input  q1,
  input  q0,
  output q2_prime
);

  wire and_1_out, not_1_out, or_1_out;

  not not_1 (not_1_out, q1);
  and and_1 (and_1_out, not_1_out, q0);
  or or_1 (or_1_out, and_1_out, q1);
  and and_2 (q2_prime, d, q2, or_1_out);
endmodule

module down_q1_logic (
  input  d,
  input  q2,
  input  q1,
  input  q0,
  output q1_prime
);

  wire and_1_out, and_2_out, not_1_out, or_1_out, xnor_1_out;

  not not_1 (not_1_out, q2);
  and and_1 (and_1_out, not_1_out, q1, q0);
  and and_2 (and_2_out, q2, xnor_1_out);
  xnor xnor_1 (xnor_1_out, q1, q0);
  or or_1 (or_1_out, and_1_out, and_2_out);
  and and_3 (q1_prime, d, or_1_out);
endmodule

module down_q0_logic (
  input  d,
  input  q2,
  input  q1,
  input  q0,
  output q0_prime
);

  wire and_1_out, not_1_out, not_2_out, or_1_out;

  not not_1 (not_1_out, q2);
  and and_1 (and_1_out, not_1_out, q1);
  or or_1 (or_1_out, q2, and_1_out);
  not not_2 (not_2_out, q0);
  and and_2 (q0_prime, d, not_2_out, or_1_out);
endmodule

module q2_logic (
  input  d,
  input  in_2,
  input  q1,
  input  q0,
  output q2_prime
);

  wire and_1_out, not_1_out, not_2_out, or_1_out;

  not not_1 (not_1_out, in_2);
  and and_1 (and_1_out, not_1_out, q1, q0);
  not not_2 (not_2_out, d);
  and and_2 (q2_prime, not_2_out, or_1_out);
  or or_1 (or_1_out, and_1_out, in_2);
endmodule

module q1_logic (
  input  d,
  input  q2,
  input  q1,
  input  q0,
  output q1_prime
);

  wire and_1_out, and_2_out, and_3_out, not_1_out, not_2_out, not_3_out, or_1_out;

  and and_1 (and_1_out, q2, q1, q0);
  not not_1 (not_1_out, q1);
  and and_2 (and_2_out, not_1_out, q0);
  and and_3 (and_3_out, q1, not_2_out);
  not not_2 (not_2_out, q0);
  or or_1 (or_1_out, and_1_out, and_2_out, and_3_out);
  not not_3 (not_3_out, d);
  and and_4 (q1_prime, not_3_out, or_1_out);
endmodule

module q0_logic (
  input  d,
  input  q2,
  input  q1,
  input  q0,
  output q0_prime
);

  wire and_1_out, and_2_out, and_3_out, and_4_out, and_5_out, not_1_out, not_2_out, not_3_out, not_4_out,
       not_5_out, not_6_out, or_1_out, or_2_out;

  not not_1 (not_1_out, q1);
  not not_2 (not_2_out, q0);
  not not_3 (not_3_out, q0);
  and and_1 (and_1_out, not_1_out, not_2_out);
  and and_2 (and_2_out, q1, not_3_out);
  or or_1 (or_1_out, and_1_out, and_2_out, and_3_out);
  and and_3 (and_3_out, q1, q0);
  not not_4 (not_4_out, d);
  not not_5 (not_5_out, q2);
  and and_4 (and_4_out, not_5_out, not_6_out);
  not not_6 (not_6_out, q0);
  and and_5 (and_5_out, q2, or_1_out);
  and and_6 (q0_prime, not_4_out, or_2_out);
  or or_2 (or_2_out, and_4_out, and_5_out);
endmodule

module top_logic (
  input  q2,
  input  q1,
  input  q0,
  output top
);

  wire and_1_out, and_2_out, and_3_out, not_1_out, not_2_out, or_1_out;

  not not_1 (not_1_out, q1);
  and and_1 (and_1_out, not_1_out, q0);
  and and_2 (and_2_out, q2, or_1_out);
  or or_1 (or_1_out, q1, and_1_out);
  not not_2 (not_2_out, q2);
  and and_3 (and_3_out, not_2_out, q1);
  or or_2 (top, and_3_out, and_2_out);
endmodule

module ltop_logic (
  input  q2,
  input  q1,
  input  q0,
  output ltop
);

  wire and_1_out, not_1_out, not_2_out, or_1_out;

  not not_1 (not_1_out, q0);
  not not_2 (not_2_out, q1);
  and and_1 (and_1_out, q1, not_1_out);
  and and_2 (ltop, q2, or_1_out);
  or or_1 (or_1_out, not_2_out, and_1_out);
endmodule

module rtop_logic (
  input  q2,
  input  q1,
  input  q0,
  output ltop
);

  wire and_1_out, and_2_out, and_3_out, not_1_out, not_2_out, or_1_out, xnor_1_out;

  not not_1 (not_1_out, q1);
  and and_1 (and_1_out, not_1_out, q0);
  not not_2 (not_2_out, q2);
  and and_2 (and_2_out, not_2_out, or_1_out);
  or or_1 (or_1_out, q1, and_1_out);
  xnor xnor_1 (xnor_1_out, q1, q0);
  or or_2 (ltop, and_2_out, and_3_out);
  and and_3 (and_3_out, q2, xnor_1_out);
endmodule

module mid_logic (
  input  q2,
  input  q1,
  input  q0,
  output mid
);

  wire and_1_out, and_2_out, not_1_out, not_2_out;

  and and_1 (and_1_out, q2, q1, q0);
  not not_1 (not_1_out, q2);
  and and_2 (and_2_out, not_1_out, not_2_out);
  not not_2 (not_2_out, q1);
  nor nor_1 (mid, and_1_out, and_2_out);
endmodule

module lbot_logic (
  input  q2,
  input  q1,
  input  q0,
  output lbot
);

  wire not_1_out;

  and and_1 (lbot, q1, not_1_out);
  not not_1 (not_1_out, q0);
endmodule

module rbot_logic (
  input  q2,
  input  q1,
  input  q0,
  output rbot
);

  wire not_1_out, not_2_out;

  not not_1 (not_1_out, q2);
  nand nand_1 (rbot, not_1_out, not_2_out);
  not not_2 (not_2_out, q0);
endmodule

module bot_logic (
  input  q2,
  input  q1,
  input  q0,
  output lbot
);

  wire and_1_out, and_2_out, not_1_out, xor_1_out;

  xor xor_1 (xor_1_out, q1, q0);
  not not_1 (not_1_out, q2);
  and and_1 (and_1_out, not_1_out, q1);
  and and_2 (and_2_out, q2, xor_1_out);
  or or_1 (lbot, and_1_out, and_2_out);
endmodule
