// Logisim project 4bit-flipper.circ as structural Verilog: 2 circuits, main circuit main
module main (
  input  [3:0] in,
  input  flip,
  output [3:0] out
);

  wire [3:0] not_1_out;

  assign not_1_out = ~in;  // NOT_Gate not_1, 4 bits wide
  _4mux2 u_4mux2_1 (.line0(in), .line1(not_1_out), .select(flip), .out(out));
endmodule

module _4mux2 (
  input  [3:0] line0,
  input  [3:0] line1,
  input  select,
  output [3:0] out
);

  wire [3:0] and_1_out, and_2_out, not_1_out;

  assign not_1_out = ~{4{select}};  // NOT_Gate not_1, 4 bits wide
  assign and_1_out = line0 & not_1_out;  // AND_Gate and_1, 4 bits wide
  assign and_2_out = line1 & {4{select}};  // AND_Gate and_2, 4 bits wide
  assign out = and_1_out | and_2_out;  // OR_Gate or_1, 4 bits wide
endmodule
