// Logisim project alu1.circ as structural Verilog: 6 circuits, main circuit parity3
module main (
  input  [3:0] x,
  input  [3:0] y,
  input  flip_x,
  input  zero_y,
  input  flip_y,
  input  add_1,
  output [3:0] z
);

  wire [3:0] _2_1_MUX_out, flipper_2_out, flipper_out;

  _4flip flipper (.in(x), .flip(flip_x), .out(flipper_out));
  _4mux2 _2_1_MUX (.line0(y), .line1(4'b0000), .select(zero_y), .out(_2_1_MUX_out));
  _4flip flipper_2 (.in(_2_1_MUX_out), .flip(flip_y), .out(flipper_2_out));
  _4fa _4_bit_adder (.x(flipper_out), .y(flipper_2_out), .cin(add_1), .z(z));  // open: cout

  // Notes on the sheet:
  //   Cin
endmodule

module _4flip (
  input  [3:0] in,
  input  flip,
  output [3:0] out
);

  wire [3:0] not_1_out;

  assign not_1_out = ~in;  // NOT_Gate not_1, 4 bits wide
  _4mux2 u_4mux2_1 (.line0(in), .line1(not_1_out), .select(flip), .out(out));
endmodule

module _4fa (
  input  cin,
  input  [3:0] x,
  input  [3:0] y,
  output [3:0] z,
  output cout
);

  wire n1fa_1_cout, n1fa_2_cout, n1fa_3_cout;

  _1fa u_1fa_1 (.cin(cin), .x(x[0]), .y(y[0]), .z(z[0]), .cout(n1fa_1_cout));
  _1fa u_1fa_2 (.cin(n1fa_1_cout), .x(x[1]), .y(y[1]), .z(z[1]), .cout(n1fa_2_cout));
  _1fa u_1fa_3 (.cin(n1fa_2_cout), .x(x[2]), .y(y[2]), .z(z[2]), .cout(n1fa_3_cout));
  _1fa u_1fa_4 (.cin(n1fa_3_cout), .x(x[3]), .y(y[3]), .z(z[3]), .cout(cout));
endmodule

module _4mux2 (
  input  [3:0] line0,
  input  [3:0] line1,
  input  select,
  output [3:0] out
);

  wire [3:0] and_1_out, and_2_out, not_1_out;

  assign not_1_out = ~{4{select}};  // NOT_Gate not_1, 4 bits wide
  assign and_1_out = line0 & not_1_out;  // AND_Gate and_1, 4 bits wide
  assign and_2_out = line1 & {4{select}};  // AND_Gate and_2, 4 bits wide
  assign out = and_1_out | and_2_out;  // OR_Gate or_1, 4 bits wide
endmodule

module _1fa (
  input  cin,
  input  x,
  input  y,
  output z,
  output cout
);

  wire and_1_out, and_2_out, and_3_out;

  parity3 parity3_1 (.x(cin), .y(x), .z(y), .parity(z));
  and and_1 (and_1_out, cin, x);
  and and_2 (and_2_out, x, y);
  and and_3 (and_3_out, cin, y);
  or or_1 (cout, and_1_out, and_2_out, and_3_out);
endmodule

module parity3 (
  input  x,
  input  y,
  input  z,
  output parity
);

  wire and_1_out, and_2_out, and_3_out, and_4_out, not_1_out, not_2_out, not_3_out, not_4_out, not_5_out,
       not_6_out;

  not not_1 (not_1_out, y);
  not not_2 (not_2_out, z);
  not not_3 (not_3_out, x);
  not not_4 (not_4_out, z);
  not not_5 (not_5_out, x);
  not not_6 (not_6_out, y);
  and and_1 (and_1_out, x, not_1_out, not_2_out);
  and and_2 (and_2_out, not_3_out, y, not_4_out);
  and and_3 (and_3_out, not_5_out, not_6_out, z);
  or or_1 (parity, and_1_out, and_2_out, and_3_out, and_4_out);
  and and_4 (and_4_out, x, y, z);
endmodule
