// Logisim project less.circ as structural Verilog: 1 circuit, main circuit main
module main (
  input  x2,
  input  x1,
  input  x0,
  input  y2,
  input  xy1,
  input  y0,
  output out_7
);

  wire and_1_out, and_2_out, and_3_out, and_4_out, and_5_out, not_1_out, not_2_out, not_3_out, xnor_1_out,
       xnor_2_out, xnor_3_out;

  not not_1 (not_1_out, x2);
  xnor xnor_1 (xnor_1_out, x2, y2);
  not not_2 (not_2_out, x1);
  and and_1 (and_1_out, not_2_out, xy1);
  not not_3 (not_3_out, x0);
  and and_2 (and_2_out, not_1_out, y2);
  and and_3 (and_3_out, xnor_1_out, and_1_out);
  xnor xnor_2 (xnor_2_out, x2, y2);
  and and_4 (and_4_out, xnor_2_out, xnor_3_out, and_5_out);
  xnor xnor_3 (xnor_3_out, x1, xy1);
  and and_5 (and_5_out, not_3_out, y0);
  or or_1 (out_7, and_2_out, and_3_out, and_4_out);
endmodule
